// Logisim project SnakeGame.circ as structural Verilog: 8 circuits, main circuit main
module main (
);

  wire CLK, clk64, clock_1_out, clock_3_out, controle_1_horizon_verti, controle_1_left_right,
       controle_1_up_down, down, gpu, left, reset, right, up;
  wire [3:0] cnt, relogio_1_out_4, relogio_1_out_5, relogio_1_out_6, relogio_1_out_7, x, y;
  wire [6:0] wasd;
  wire [15:0] gpu_1_out_3, gpu_1_out_4, gpu_1_out_5, gpu_1_out_6, gpu_1_out_7, gpu_1_out_8, gpu_1_out_9,
       gpu_1_out_10, gpu_1_out_11, gpu_1_out_12, gpu_1_out_13, gpu_1_out_14, gpu_1_out_15, gpu_1_out_16,
       gpu_1_out_17, gpu_1_out_18;

  Keyboard keyboard_1 (.clr(clock_1_out), .data(wasd));  // open: clk, re, avail
  Clock #(.lowDuration(10)) clock_1 (.out(clock_1_out));
  Clock clock_2 (.out(clk64));
  controle controle_1 (
    .horizon_verti(controle_1_horizon_verti), .up_down(controle_1_up_down),
    .left_right(controle_1_left_right), .up(up), .down(down), .left(left), .right(right));
  mov_do_dot mov_do_dot_1 (
    .Y(x), .X(y), .left_right(controle_1_left_right), .up_down(controle_1_up_down),
    .direction(controle_1_horizon_verti), .in_1(CLK));
  teclado teclado_1 (.a(left), .w(up), .s(down), .d(right), .in_1(wasd));
  DotMatrix #(.matrixcols(16), .matrixrows(16), .persist(10)) dotmatrix_1 (
    .col0(gpu_1_out_3), .col1(gpu_1_out_4), .col2(gpu_1_out_5), .col3(gpu_1_out_6), .col4(gpu_1_out_7),
    .col5(gpu_1_out_8), .col6(gpu_1_out_9), .col7(gpu_1_out_10), .col8(gpu_1_out_11), .col9(gpu_1_out_12),
    .col10(gpu_1_out_13), .col11(gpu_1_out_14), .col12(gpu_1_out_15), .col13(gpu_1_out_16),
    .col14(gpu_1_out_17), .col15(gpu_1_out_18));
  gpu gpu_1 (
    .out_3(gpu_1_out_3), .out_4(gpu_1_out_4), .out_5(gpu_1_out_5), .out_6(gpu_1_out_6), .out_7(gpu_1_out_7),
    .out_8(gpu_1_out_8), .out_9(gpu_1_out_9), .out_10(gpu_1_out_10), .out_11(gpu_1_out_11),
    .out_12(gpu_1_out_12), .out_13(gpu_1_out_13), .out_14(gpu_1_out_14), .out_15(gpu_1_out_15),
    .out_16(gpu_1_out_16), .out_17(gpu_1_out_17), .out_18(gpu_1_out_18), .X(x), .out_19(gpu), .Y(y));
  Button u_reset (.out(reset));
  contador contador_1 (.in_2(gpu), .reset(reset), .out_3(cnt));
  Hex_Digit_Display hex_digit_display_1 (.value(cnt));  // open: dp
  reduzir reduzir_1 (.in_2(clk64), .contador_de_fruta(cnt), .novo_clock(CLK));
  Hex_Digit_Display hex_digit_display_2 (.value(relogio_1_out_7));  // open: dp
  Hex_Digit_Display hex_digit_display_3 (.value(relogio_1_out_4));  // open: dp
  relogio relogio_1 (
    .in_3(reset), .out_7(relogio_1_out_7), .out_4(relogio_1_out_4), .out_5(relogio_1_out_5),
    .out_6(relogio_1_out_6), .clk(clock_3_out), .in_1(cnt));
  LED led_1 ();  // open: in
  LED led_2 ();  // open: in
  Hex_Digit_Display hex_digit_display_4 (.value(relogio_1_out_5));  // open: dp
  Clock #(.highDuration(64)) clock_3 (.out(clock_3_out));
  Hex_Digit_Display hex_digit_display_5 (.value(relogio_1_out_6));  // open: dp

  // Notes on the sheet:
  //   TECLADO
  //   mov do dot
  //   controle
  //   Teclado
  //   PLACAR
  //   CRONOMETRO
  //   Relógio
endmodule

// GPU
module gpu (
  input  [3:0] X,
  input  [3:0] Y,
  output [15:0] out_3,
  output [15:0] out_4,
  output [15:0] out_5,
  output [15:0] out_6,
  output [15:0] out_7,
  output [15:0] out_8,
  output [15:0] out_9,
  output [15:0] out_10,
  output [15:0] out_11,
  output [15:0] out_12,
  output [15:0] out_13,
  output [15:0] out_14,
  output [15:0] out_15,
  output [15:0] out_16,
  output [15:0] out_17,
  output [15:0] out_18,
  output out_19
);

  wire comparator_1_eq, comparator_2_eq;
  wire [3:0] random_1_out, random_2_out;
  wire [15:0] _0, _1, _2, _3, _4, _5, _6, _7, _8, _9, A, B, C, D, demultiplexer_1_out0, demultiplexer_3_out0,
       demultiplexer_4_out0, demultiplexer_4_out1, demultiplexer_4_out2, demultiplexer_4_out3,
       demultiplexer_4_out4, demultiplexer_4_out5, demultiplexer_4_out6, demultiplexer_4_out7,
       demultiplexer_4_out8, demultiplexer_4_out9, demultiplexer_4_out10, demultiplexer_4_out11,
       demultiplexer_4_out12, demultiplexer_4_out13, demultiplexer_4_out14, demultiplexer_4_out15, E, F;

  assign out_3 = demultiplexer_4_out0 | _0;  // OR_Gate or_1, 16 bits wide
  assign out_4 = demultiplexer_4_out1 | _1;  // OR_Gate or_2, 16 bits wide
  Demultiplexer #(.select(4), .enable("false")) demultiplexer_1 (
    .out0(demultiplexer_1_out0[0]), .out1(demultiplexer_1_out0[1]), .out2(demultiplexer_1_out0[2]),
    .out3(demultiplexer_1_out0[3]), .out4(demultiplexer_1_out0[4]), .out5(demultiplexer_1_out0[5]),
    .out6(demultiplexer_1_out0[6]), .out7(demultiplexer_1_out0[7]), .out8(demultiplexer_1_out0[8]),
    .out9(demultiplexer_1_out0[9]), .out10(demultiplexer_1_out0[10]), .out11(demultiplexer_1_out0[11]),
    .out12(demultiplexer_1_out0[12]), .out13(demultiplexer_1_out0[13]), .out14(demultiplexer_1_out0[14]),
    .out15(demultiplexer_1_out0[15]), .sel(random_1_out));  // open: in
  Random #(.width(4)) random_1 (.clk(out_19), .out(random_1_out));  // open: next, clr
  Random #(.width(4)) random_2 (.clk(out_19), .out(random_2_out));  // open: next, clr
  assign out_5 = demultiplexer_4_out2 | _2;  // OR_Gate or_3, 16 bits wide
  Demultiplexer #(.select(4), .width(16), .enable("false")) demultiplexer_2 (
    .out0(_0), .out1(_1), .out2(_2), .out3(_3), .out4(_4), .out5(_5), .out6(_6), .out7(_7), .out8(_8),
    .out9(_9), .out10(A), .out11(B), .out12(C), .out13(D), .out14(E), .out15(F), .in(demultiplexer_1_out0),
    .sel(random_2_out));
  assign out_6 = demultiplexer_4_out3 | _3;  // OR_Gate or_4, 16 bits wide
  assign out_7 = demultiplexer_4_out4 | _4;  // OR_Gate or_5, 16 bits wide
  Demultiplexer #(.select(4), .enable("false")) demultiplexer_3 (
    .out0(demultiplexer_3_out0[0]), .out1(demultiplexer_3_out0[1]), .out2(demultiplexer_3_out0[2]),
    .out3(demultiplexer_3_out0[3]), .out4(demultiplexer_3_out0[4]), .out5(demultiplexer_3_out0[5]),
    .out6(demultiplexer_3_out0[6]), .out7(demultiplexer_3_out0[7]), .out8(demultiplexer_3_out0[8]),
    .out9(demultiplexer_3_out0[9]), .out10(demultiplexer_3_out0[10]), .out11(demultiplexer_3_out0[11]),
    .out12(demultiplexer_3_out0[12]), .out13(demultiplexer_3_out0[13]), .out14(demultiplexer_3_out0[14]),
    .out15(demultiplexer_3_out0[15]), .in(1'b1), .sel(X));
  Comparator #(.width(4)) comparator_1 (.a(X), .b(random_1_out), .eq(comparator_1_eq));  // open: gt, lt
  Comparator #(.width(4)) comparator_2 (.a(Y), .b(random_2_out), .eq(comparator_2_eq));  // open: gt, lt
  assign out_8 = demultiplexer_4_out5 | _5;  // OR_Gate or_6, 16 bits wide
  and and_1 (out_19, comparator_1_eq, comparator_2_eq);
  assign out_9 = demultiplexer_4_out6 | _6;  // OR_Gate or_7, 16 bits wide
  assign out_10 = demultiplexer_4_out7 | _7;  // OR_Gate or_8, 16 bits wide
  Demultiplexer #(.select(4), .width(16), .enable("false")) demultiplexer_4 (
    .out0(demultiplexer_4_out0), .out1(demultiplexer_4_out1), .out2(demultiplexer_4_out2),
    .out3(demultiplexer_4_out3), .out4(demultiplexer_4_out4), .out5(demultiplexer_4_out5),
    .out6(demultiplexer_4_out6), .out7(demultiplexer_4_out7), .out8(demultiplexer_4_out8),
    .out9(demultiplexer_4_out9), .out10(demultiplexer_4_out10), .out11(demultiplexer_4_out11),
    .out12(demultiplexer_4_out12), .out13(demultiplexer_4_out13), .out14(demultiplexer_4_out14),
    .out15(demultiplexer_4_out15), .in(demultiplexer_3_out0), .sel(Y));
  assign out_11 = demultiplexer_4_out8 | _8;  // OR_Gate or_9, 16 bits wide
  assign out_12 = demultiplexer_4_out9 | _9;  // OR_Gate or_10, 16 bits wide
  assign out_13 = demultiplexer_4_out10 | A;  // OR_Gate or_11, 16 bits wide
  assign out_14 = demultiplexer_4_out11 | B;  // OR_Gate or_12, 16 bits wide
  assign out_15 = demultiplexer_4_out12 | C;  // OR_Gate or_13, 16 bits wide
  assign out_16 = demultiplexer_4_out13 | D;  // OR_Gate or_14, 16 bits wide
  assign out_17 = demultiplexer_4_out14 | E;  // OR_Gate or_15, 16 bits wide
  assign out_18 = demultiplexer_4_out15 | F;  // OR_Gate or_16, 16 bits wide

  // Notes on the sheet:
  //   cobra ta na msm posiçao da fruta
endmodule

module mov_do_dot (
  input  in_1,
  input  left_right,
  input  up_down,
  input  direction,
  output [3:0] Y,
  output [3:0] X
);

  wire not_1_out;
  wire [3:0] adder_1_out, adder_2_out, multiplexer_1_out, multiplexer_2_out;

  Multiplexer #(.width(4), .enable("false")) multiplexer_1 (
    .in0(4'b0001), .in1(4'b1111), .out(multiplexer_1_out), .sel(left_right));
  Multiplexer #(.width(4), .enable("false")) multiplexer_2 (
    .in0(4'b0001), .in1(4'b1111), .out(multiplexer_2_out), .sel(up_down));
  Adder #(.width(4)) adder_1 (.a(Y), .b(multiplexer_2_out), .out(adder_1_out));  // open: cin, cout
  Adder #(.width(4)) adder_2 (.a(X), .b(multiplexer_1_out), .out(adder_2_out));  // open: cin, cout
  not not_1 (not_1_out, direction);
  Register #(.width(4), .Select("low")) u_Y (.D(adder_1_out), .en(direction), .Q(Y), .clk(in_1));  // open: clr
  Register #(.width(4), .Select("low")) u_X (.D(adder_2_out), .en(not_1_out), .Q(X), .clk(in_1));  // open: clr

  // Other names for the same wires on the sheet: CLK = in_1

  // Notes on the sheet:
  //   p ativar x (horizontal)  desabilita y
endmodule

module controle (
  input  up,
  input  down,
  input  left,
  input  right,
  output horizon_verti,
  output up_down,
  output left_right
);

  wire clk, d_ff_1_q, d_ff_2_q, d_ff_3_q, d_ff_4_q, or_2_out, or_3_out, or_5_out, or_7_out;

  or or_1 (horizon_verti, d_ff_1_q, d_ff_2_q);
  D_Flip_Flop d_ff_1 (.clk(clk), .Q(d_ff_1_q), .preset(up), .reset(or_2_out));  // open: D, Qn
  or or_2 (or_2_out, down, left, right);
  or or_3 (or_3_out, up, left, right);
  or or_4 (up_down, ~d_ff_1_q, d_ff_2_q);  // OR_Gate
  D_Flip_Flop d_ff_2 (.clk(clk), .Q(d_ff_2_q), .preset(down), .reset(or_3_out));  // open: D, Qn
  D_Flip_Flop d_ff_3 (.clk(clk), .Q(d_ff_3_q), .preset(left), .reset(or_5_out));  // open: D, Qn
  or or_5 (or_5_out, up, down, right);
  or or_6 (left_right, d_ff_3_q, ~d_ff_4_q);  // OR_Gate
  D_Flip_Flop d_ff_4 (.clk(clk), .Q(d_ff_4_q), .preset(right), .reset(or_7_out));  // open: D, Qn
  or or_7 (or_7_out, up, down, left);
endmodule

module contador (
  input  reset,
  input  in_2,
  output [3:0] out_3
);

  wire [3:0] adder_1_out;

  Adder #(.width(4)) adder_1 (.a(out_3), .b(4'b0001), .out(adder_1_out));  // open: cin, cout
  Register #(.width(4), .Select("low")) Y (.D(adder_1_out), .Q(out_3), .clk(in_2), .clr(reset));  // open: en
endmodule

module reduzir (
  input  [3:0] contador_de_fruta,
  input  in_2,
  output novo_clock
);

  wire and_1_out, and_2_out, and_3_out, and_4_out, and_5_out, comparator_1_eq, comparator_2_eq,
       comparator_3_eq, comparator_4_eq, comparator_5_eq, j_k_ff_1_q, j_k_ff_2_q, j_k_ff_3_q, j_k_ff_4_q;

  J_K_Flip_Flop j_k_ff_1 (.J(1'b1), .clk(in_2), .K(1'b1), .Q(j_k_ff_1_q));  // open: Qn, preset, reset
  Comparator #(.width(4)) comparator_1 (.a(contador_de_fruta), .b(4'b0100), .eq(comparator_1_eq));  // open: gt, lt
  Comparator #(.width(4)) comparator_2 (.a(contador_de_fruta), .b(4'b0011), .eq(comparator_2_eq));  // open: gt, lt
  Comparator #(.width(4)) comparator_3 (.a(contador_de_fruta), .b(4'b0010), .eq(comparator_3_eq));  // open: gt, lt
  Comparator #(.width(4)) comparator_4 (.a(contador_de_fruta), .b(4'b0001), .eq(comparator_4_eq));  // open: gt, lt
  Comparator #(.width(4)) comparator_5 (.a(contador_de_fruta), .b(4'b0000), .eq(comparator_5_eq));  // open: gt, lt
  J_K_Flip_Flop j_k_ff_2 (.J(1'b1), .clk(j_k_ff_1_q), .K(1'b1), .Q(j_k_ff_2_q));  // open: Qn, preset, reset
  J_K_Flip_Flop j_k_ff_3 (.J(1'b1), .clk(j_k_ff_2_q), .K(1'b1), .Q(j_k_ff_3_q));  // open: Qn, preset, reset
  and and_1 (and_1_out, in_2, comparator_1_eq);
  and and_2 (and_2_out, j_k_ff_1_q, comparator_2_eq);
  and and_3 (and_3_out, j_k_ff_2_q, comparator_3_eq);
  and and_4 (and_4_out, j_k_ff_3_q, comparator_4_eq);
  and and_5 (and_5_out, j_k_ff_4_q, comparator_5_eq);
  J_K_Flip_Flop j_k_ff_4 (.J(1'b1), .clk(j_k_ff_3_q), .K(1'b1), .Q(j_k_ff_4_q));  // open: Qn, preset, reset
  or or_1 (novo_clock, and_1_out, and_2_out, and_3_out, and_4_out, and_5_out);

  // Notes on the sheet:
  //   64 Hz
  //   32 Hz
  //   16 Hz
  //   8 Hz
  //   4 Hz
endmodule

module relogio (
  input  [3:0] in_1,
  input  clk,
  input  in_3,
  output [3:0] out_4,
  output [3:0] out_5,
  output [3:0] out_6,
  output [3:0] out_7
);

  wire and_1_out, comparator_1_eq, nor_1_out, nor_2_out, nor_3_out, nor_4_out, OR_2_out, OR_3_out, OR_4_out,
       OR_out;
  wire [3:0] adder_1_out, adder_2_out, adder_3_out, adder_4_out;

  Register #(.width(4), .Select("low")) register_1 (
    .D(adder_1_out), .Q(out_7), .clk(OR_2_out), .clr(OR_out));  // open: en
  Hex_Digit_Display hex_digit_display_1 (.value(out_7));  // open: dp
  or OR (OR_out, nor_1_out, in_3);
  Adder #(.width(4)) adder_1 (.a(out_7), .b(4'b0001), .out(adder_1_out));  // open: cin, cout
  nor nor_1 (nor_1_out, out_7[0], ~out_7[1], ~out_7[2], out_7[3]);  // NOR_Gate
  Register #(.width(4), .Select("low")) register_2 (.D(adder_2_out), .Q(out_4), .clr(OR_2_out));  // open: en, clk
  Hex_Digit_Display hex_digit_display_2 (.value(out_4));  // open: dp
  or OR_2 (OR_2_out, nor_2_out, in_3);
  Adder #(.width(4)) adder_2 (.a(out_4), .b(4'b0001), .out(adder_2_out));  // open: cin, cout
  nor nor_2 (nor_2_out, out_4[0], ~out_4[1], out_4[2], ~out_4[3]);  // NOR_Gate
  Register #(.width(4), .Select("low")) register_3 (
    .D(adder_3_out), .Q(out_5), .clk(OR_4_out), .clr(OR_3_out));  // open: en
  Hex_Digit_Display hex_digit_display_3 (.value(out_5));  // open: dp
  or OR_3 (OR_3_out, nor_3_out, in_3);
  Adder #(.width(4)) adder_3 (.a(out_5), .b(4'b0001), .out(adder_3_out));  // open: cin, cout
  Comparator #(.width(4)) comparator_1 (.a(in_1), .b(4'b0101), .eq(comparator_1_eq));  // open: gt, lt
  and and_1 (and_1_out, ~comparator_1_eq, clk);  // AND_Gate
  nor nor_3 (nor_3_out, out_5[0], ~out_5[1], ~out_5[2], out_5[3]);  // NOR_Gate
  Register #(.width(4), .Select("low")) register_4 (
    .D(adder_4_out), .Q(out_6), .clk(and_1_out), .clr(OR_4_out));  // open: en
  Hex_Digit_Display hex_digit_display_4 (.value(out_6));  // open: dp
  or OR_4 (OR_4_out, nor_4_out, in_3);
  Adder #(.width(4)) adder_4 (.a(out_6), .b(4'b0001), .out(adder_4_out));  // open: cin, cout
  nor nor_4 (nor_4_out, out_6[0], ~out_6[1], out_6[2], ~out_6[3]);  // NOR_Gate
endmodule

module teclado (
  input  [6:0] in_1,
  output a,
  output w,
  output s,
  output d
);

  Comparator #(.width(7)) comparator_1 (.a(in_1), .b(7'b1100001), .eq(a));  // open: gt, lt
  Comparator #(.width(7)) comparator_2 (.a(in_1), .b(7'b1110111), .eq(w));  // open: gt, lt
  Comparator #(.width(7)) comparator_3 (.a(in_1), .b(7'b1110011), .eq(s));  // open: gt, lt
  Comparator #(.width(7)) comparator_4 (.a(in_1), .b(7'b1100100), .eq(d));  // open: gt, lt
endmodule
